// Logisim project logiregister.circ as structural Verilog: 1 circuit, main circuit main
module main (
  input  in_1,
  input  in_2,
  input  in_3,
  input  X,
  output Y
);

  wire clock_1_out, decoder_1_out0, decoder_1_out1, decoder_1_out2, decoder_1_out3, decoder_1_out4,
       decoder_1_out5, decoder_1_out6, decoder_1_out7, decoder_1_out8, decoder_1_out9, decoder_1_out10,
       decoder_1_out11, decoder_1_out12, decoder_1_out13;
  wire [2:0] or_2_out;
  wire [3:0] d_ff_1_q;

  Decoder #(.select(4)) decoder_1 (
    .out0(decoder_1_out0), .out1(decoder_1_out1), .out2(decoder_1_out2), .out3(decoder_1_out3),
    .out4(decoder_1_out4), .out5(decoder_1_out5), .out6(decoder_1_out6), .out7(decoder_1_out7),
    .out8(decoder_1_out8), .out9(decoder_1_out9), .out10(decoder_1_out10), .out11(decoder_1_out11),
    .out12(decoder_1_out12), .out13(decoder_1_out13), .sel(d_ff_1_q), .en(in_3));  // open: out14, out15
  or or_1 (Y, decoder_1_out6, decoder_1_out13);
  or or_2 (or_2_out[0], decoder_1_out12, decoder_1_out10, decoder_1_out9, decoder_1_out8, decoder_1_out6, decoder_1_out4, decoder_1_out0);
  or or_3 (or_2_out[1], decoder_1_out2, decoder_1_out4, decoder_1_out6, decoder_1_out11, decoder_1_out13);
  or or_4 (or_2_out[2], decoder_1_out1, decoder_1_out3, decoder_1_out5, decoder_1_out7, decoder_1_out9, decoder_1_out11, decoder_1_out13);
  D_Flip_Flop d_ff_1 (.clk(clock_1_out), .D(X), .Q(d_ff_1_q[0]));  // open: Qn, preset, en, reset
  Register #(.width(3)) register_1 (.D(or_2_out), .en(in_1), .Q(d_ff_1_q[3:1]), .clk(clock_1_out), .clr(in_2));
  Clock clock_1 (.out(clock_1_out));
endmodule
